// Logisim project JizuLab.circ as structural Verilog: 6 circuits, main circuit main
module main (
  input  [7:0] in_1,
  input  [1:0] in_2
);

  wire decoder_1_a, decoder_1_b, decoder_1_c, decoder_1_d, decoder_1_e, decoder_1_f, decoder_1_g,
       decoder_2_a, decoder_2_b, decoder_2_c, decoder_2_d, decoder_2_e, decoder_2_f, decoder_2_g,
       decoder_3_a, decoder_3_b, decoder_3_c, decoder_3_d, decoder_3_e, decoder_3_f, decoder_3_g,
       decoder_4_a, decoder_4_b, decoder_4_c, decoder_4_d, decoder_4_e, decoder_4_f, decoder_4_g,
       decoder_5_a, decoder_5_b, decoder_5_c, decoder_5_d, decoder_5_e, decoder_5_f, decoder_5_g,
       decoder_6_a, decoder_6_b, decoder_6_c, decoder_6_d, decoder_6_e, decoder_6_f, decoder_6_g,
       decoder_7_a, decoder_7_b, decoder_7_c, decoder_7_d, decoder_7_e, decoder_7_f, decoder_7_g,
       decoder_8_a, decoder_8_b, decoder_8_c, decoder_8_d, decoder_8_e, decoder_8_f, decoder_8_g;
  wire [7:0] buma_1_out_2, fanma_1_out_2, multiplexer_1_out, yima_1_out_2, yuanma_1_out_2;

  decoder decoder_1 (
    .A0(multiplexer_1_out[7]), .a(decoder_1_a), .b(decoder_1_b), .c(decoder_1_c), .d(decoder_1_d),
    .e(decoder_1_e), .f(decoder_1_f), .g(decoder_1_g));  // open: A3, A2, A1
  _7_Segment_Display u_7_segment_display_1 (
    .g(decoder_1_g), .f(decoder_1_f), .a(decoder_1_a), .b(decoder_1_b), .e(decoder_1_e), .d(decoder_1_d),
    .c(decoder_1_c));  // open: dp
  decoder decoder_2 (
    .A0(multiplexer_1_out[6]), .a(decoder_2_a), .b(decoder_2_b), .c(decoder_2_c), .d(decoder_2_d),
    .e(decoder_2_e), .f(decoder_2_f), .g(decoder_2_g));  // open: A3, A2, A1
  _7_Segment_Display u_7_segment_display_2 (
    .g(decoder_2_g), .f(decoder_2_f), .a(decoder_2_a), .b(decoder_2_b), .e(decoder_2_e), .d(decoder_2_d),
    .c(decoder_2_c));  // open: dp
  // Probe on yuanma_1_out_2
  decoder decoder_3 (
    .A0(multiplexer_1_out[5]), .a(decoder_3_a), .b(decoder_3_b), .c(decoder_3_c), .d(decoder_3_d),
    .e(decoder_3_e), .f(decoder_3_f), .g(decoder_3_g));  // open: A3, A2, A1
  // Probe on fanma_1_out_2
  _7_Segment_Display u_7_segment_display_3 (
    .g(decoder_3_g), .f(decoder_3_f), .a(decoder_3_a), .b(decoder_3_b), .e(decoder_3_e), .d(decoder_3_d),
    .c(decoder_3_c));  // open: dp
  // Probe on buma_1_out_2
  decoder decoder_4 (
    .A0(multiplexer_1_out[4]), .a(decoder_4_a), .b(decoder_4_b), .c(decoder_4_c), .d(decoder_4_d),
    .e(decoder_4_e), .f(decoder_4_f), .g(decoder_4_g));  // open: A3, A2, A1
  // Probe on yima_1_out_2
  Yuanma yuanma_1 (.in_1(in_1), .out_2(yuanma_1_out_2));
  Fanma fanma_1 (.in_1(in_1), .out_2(fanma_1_out_2));
  BuMa buma_1 (.in_1(in_1), .out_2(buma_1_out_2));
  Yima yima_1 (.in_1(in_1), .out_2(yima_1_out_2));
  _7_Segment_Display u_7_segment_display_4 (
    .g(decoder_4_g), .f(decoder_4_f), .a(decoder_4_a), .b(decoder_4_b), .e(decoder_4_e), .d(decoder_4_d),
    .c(decoder_4_c));  // open: dp
  decoder decoder_5 (
    .A0(multiplexer_1_out[3]), .a(decoder_5_a), .b(decoder_5_b), .c(decoder_5_c), .d(decoder_5_d),
    .e(decoder_5_e), .f(decoder_5_f), .g(decoder_5_g));  // open: A3, A2, A1
  Multiplexer #(.select(2), .width(8)) multiplexer_1 (
    .in0(yuanma_1_out_2), .in1(fanma_1_out_2), .in2(buma_1_out_2), .in3(yima_1_out_2),
    .out(multiplexer_1_out), .sel(in_2));
  _7_Segment_Display u_7_segment_display_5 (
    .g(decoder_5_g), .f(decoder_5_f), .a(decoder_5_a), .b(decoder_5_b), .e(decoder_5_e), .d(decoder_5_d),
    .c(decoder_5_c));  // open: dp
  decoder decoder_6 (
    .A0(multiplexer_1_out[2]), .a(decoder_6_a), .b(decoder_6_b), .c(decoder_6_c), .d(decoder_6_d),
    .e(decoder_6_e), .f(decoder_6_f), .g(decoder_6_g));  // open: A3, A2, A1
  _7_Segment_Display u_7_segment_display_6 (
    .g(decoder_6_g), .f(decoder_6_f), .a(decoder_6_a), .b(decoder_6_b), .e(decoder_6_e), .d(decoder_6_d),
    .c(decoder_6_c));  // open: dp
  decoder decoder_7 (
    .A0(multiplexer_1_out[1]), .a(decoder_7_a), .b(decoder_7_b), .c(decoder_7_c), .d(decoder_7_d),
    .e(decoder_7_e), .f(decoder_7_f), .g(decoder_7_g));  // open: A3, A2, A1
  _7_Segment_Display u_7_segment_display_7 (
    .g(decoder_7_g), .f(decoder_7_f), .a(decoder_7_a), .b(decoder_7_b), .e(decoder_7_e), .d(decoder_7_d),
    .c(decoder_7_c));  // open: dp
  decoder decoder_8 (
    .A0(multiplexer_1_out[0]), .a(decoder_8_a), .b(decoder_8_b), .c(decoder_8_c), .d(decoder_8_d),
    .e(decoder_8_e), .f(decoder_8_f), .g(decoder_8_g));  // open: A3, A2, A1
  _7_Segment_Display u_7_segment_display_8 (
    .g(decoder_8_g), .f(decoder_8_f), .a(decoder_8_a), .b(decoder_8_b), .e(decoder_8_e), .d(decoder_8_d),
    .c(decoder_8_c));  // open: dp
endmodule

module BuMa (
  input  [7:0] in_1,
  output [7:0] out_2
);

  wire and_2_out, and_3_out, and_4_out, and_5_out, and_6_out, and_7_out, xor_1_out, xor_2_out, xor_3_out,
       xor_5_out, xor_6_out, xor_8_out, xor_9_out;

  xor xor_1 (xor_1_out, in_1[7], in_1[6]);
  xor xor_2 (xor_2_out, in_1[7], in_1[5]);
  xor xor_3 (xor_3_out, in_1[7], in_1[4]);
  // AND_Gate and_1 has open pins: in0=xor_1_out, in1=and_2_out, out=open
  xor xor_4 (out_2[6], xor_1_out, and_2_out);
  xor xor_5 (xor_5_out, in_1[7], in_1[3]);
  xor xor_6 (xor_6_out, in_1[7], in_1[2]);
  and and_2 (and_2_out, xor_2_out, and_3_out);
  xor xor_7 (out_2[5], xor_2_out, and_3_out);
  xor xor_8 (xor_8_out, in_1[7], in_1[1]);
  xor xor_9 (xor_9_out, in_1[7], in_1[0]);
  and and_3 (and_3_out, xor_3_out, and_4_out);
  and and_4 (and_4_out, xor_5_out, and_5_out);
  xor xor_10 (out_2[4], xor_3_out, and_4_out);
  and and_5 (and_5_out, xor_6_out, and_6_out);
  xor xor_11 (out_2[3], xor_5_out, and_5_out);
  and and_6 (and_6_out, xor_8_out, and_7_out);
  xor xor_12 (out_2[2], xor_6_out, and_6_out);
  and and_7 (and_7_out, xor_9_out, in_1[7]);
  xor xor_13 (out_2[1], xor_8_out, and_7_out);
  xor xor_14 (out_2[0], in_1[7], xor_9_out);

  assign out_2[7] = in_1[7];
endmodule

module Yuanma (
  input  [7:0] in_1,
  output [7:0] out_2
);


  assign out_2 = in_1;
endmodule

module Yima (
  input  [7:0] in_1,
  output [7:0] out_2
);

  wire and_2_out, and_3_out, and_4_out, and_5_out, and_6_out, and_7_out, xor_1_out, xor_2_out, xor_3_out,
       xor_5_out, xor_6_out, xor_8_out, xor_9_out;

  not not_1 (out_2[7], in_1[7]);
  xor xor_1 (xor_1_out, in_1[7], in_1[6]);
  xor xor_2 (xor_2_out, in_1[7], in_1[5]);
  xor xor_3 (xor_3_out, in_1[7], in_1[4]);
  // AND_Gate and_1 has open pins: in0=xor_1_out, in1=and_2_out, out=open
  xor xor_4 (out_2[6], xor_1_out, and_2_out);
  xor xor_5 (xor_5_out, in_1[7], in_1[3]);
  xor xor_6 (xor_6_out, in_1[7], in_1[2]);
  and and_2 (and_2_out, xor_2_out, and_3_out);
  xor xor_7 (out_2[5], xor_2_out, and_3_out);
  xor xor_8 (xor_8_out, in_1[7], in_1[1]);
  xor xor_9 (xor_9_out, in_1[7], in_1[0]);
  and and_3 (and_3_out, xor_3_out, and_4_out);
  and and_4 (and_4_out, xor_5_out, and_5_out);
  xor xor_10 (out_2[4], xor_3_out, and_4_out);
  and and_5 (and_5_out, xor_6_out, and_6_out);
  xor xor_11 (out_2[3], xor_5_out, and_5_out);
  and and_6 (and_6_out, xor_8_out, and_7_out);
  xor xor_12 (out_2[2], xor_6_out, and_6_out);
  and and_7 (and_7_out, xor_9_out, in_1[7]);
  xor xor_13 (out_2[1], xor_8_out, and_7_out);
  xor xor_14 (out_2[0], in_1[7], xor_9_out);
endmodule

module Fanma (
  input  [7:0] in_1,
  output [7:0] out_2
);

  xor xor_1 (out_2[6], in_1[7], in_1[6]);
  xor xor_2 (out_2[5], in_1[7], in_1[5]);
  xor xor_3 (out_2[4], in_1[7], in_1[4]);
  xor xor_4 (out_2[3], in_1[7], in_1[3]);
  xor xor_5 (out_2[2], in_1[7], in_1[2]);
  xor xor_6 (out_2[1], in_1[7], in_1[1]);
  xor xor_7 (out_2[0], in_1[7], in_1[0]);

  assign out_2[7] = in_1[7];
endmodule

module decoder (
  input  A3,
  input  A2,
  input  A1,
  input  A0,
  output a,
  output b,
  output c,
  output d,
  output e,
  output f,
  output g
);

  wire and_1_out, and_2_out, and_3_out, and_4_out, and_5_out, and_6_out, and_7_out, and_8_out, and_9_out,
       and_10_out, and_11_out, and_12_out, and_13_out, and_14_out, and_15_out, and_16_out, not_1_out,
       not_2_out, not_3_out;

  not not_1 (not_1_out, A2);
  not not_2 (not_2_out, A1);
  not not_3 (not_3_out, A0);
  and and_1 (and_1_out, not_1_out, not_3_out);
  and and_2 (and_2_out, A2, A0);
  and and_3 (and_3_out, not_2_out, not_3_out);
  and and_4 (and_4_out, A1, A0);
  or or_1 (c, not_2_out, A0, A2);
  and and_5 (and_5_out, not_1_out, not_3_out);
  and and_6 (and_6_out, not_1_out, A1);
  and and_7 (and_7_out, A2, not_2_out, A0);
  and and_8 (and_8_out, A1, not_3_out);
  and and_9 (and_9_out, not_1_out, not_3_out);
  and and_10 (and_10_out, A1, not_3_out);
  and and_11 (and_11_out, not_2_out, not_3_out);
  and and_12 (and_12_out, A2, not_2_out);
  and and_13 (and_13_out, A2, not_3_out);
  and and_14 (and_14_out, not_1_out, A1);
  and and_15 (and_15_out, A2, not_2_out);
  and and_16 (and_16_out, A1, not_3_out);
  or or_2 (a, and_1_out, A1, and_2_out, A3);
  or or_3 (b, not_1_out, and_3_out, and_4_out);
  or or_4 (d, and_5_out, and_6_out, and_7_out, and_8_out, A3);
  or or_5 (e, and_9_out, and_10_out);
  or or_6 (f, and_11_out, and_12_out, and_13_out, A3);
  or or_7 (g, and_14_out, and_15_out, A3, and_16_out);
endmodule
